# Fritzing sketch Sensor Efeito Hall - RPM e Velocidade Fritzing (saved by Fritzing 0.9.2b)
breadboards: 1

parts:
  Componente1 = Arduino Uno (Rev3)
  Q2 = NPN-Transistor [package="TO92 [THT]"]
  R1 = Resistor [tolerance=±5% resistance=220 package=THT]
  LED1 = smd LED [color="Red (633nm)" package="0603 [SMD]"]
  R2 = Resistor [tolerance=±5% resistance=220 package="2010 [SMD]"]

nets:
  N1: Componente1.D4, R2.Pin_0
  N2: Componente1.D7, Q2.C, R1.Pin_0
  N3: Componente1.5V, Q2.E, R1.Pin_1
  N4: Componente1.GND, LED1.cathode
  N5: LED1.anode, R2.Pin_1
